# Fritzing sketch Untitled Sketch 2 (saved by Fritzing 0.9.3b)
breadboards: 1

parts:
  LED1 = LED - 5mm [color="Red (633nm)" package="5 mm [THT]"]
  LED2 = LED - 5mm [color="Red (633nm)" package="5 mm [THT]"]
  LED3 = LED - 5mm [color="Red (633nm)" package="5 mm [THT]"]
  R1 = Resistor [tolerance=±5% resistance=220 package=THT]
  R2 = Resistor [tolerance=±5% resistance=220 package=THT]
  R3 = Resistor [tolerance=±5% resistance=220 package=THT]
  IOXESP32PS1 = IOXESP32PS [part_number=IOXESP32 chip_label=IOXESP32PS package="DIP (Dual Inline) [THT]"]
  S1 = H-Bridge with L298N
  Part1 = FC-28 Soil Hygrometer Module - Probe
  M3 = DC Motor
  Part2 = FC-28 Soil Hygrometer Module
  Mod1 = KY-012 Active Buzzer Module [package="Breakout board"]
  A1 = Hanmatek HM305

nets:
  GND: LED1.cathode, LED2.cathode, LED3.cathode, IOXESP32PS1.GND#55, S1.GND, Part2.GND, Mod1.-, A1.Pin_3
  N1: LED1.anode, R1.Pin_0
  N2: LED2.anode, R2.Pin_0
  N3: LED3.anode, R3.Pin_0
  N4: R1.Pin_1, IOXESP32PS1.NC1
  N5: R2.Pin_1, IOXESP32PS1.IO4
  N6: R3.Pin_1, IOXESP32PS1.IO0
  3V3: IOXESP32PS1.3V3, Part2.VCC, Mod1.S
  N7: IOXESP32PS1.IO36, Part2.AO
  N8: IOXESP32PS1.IO15, Mod1.NC
  N9: IOXESP32PS1.IO18, S1.IN2
  N10: IOXESP32PS1.IO19, S1.IN3
  N11: S1.12V, A1.Pin_4
  N12: S1.M1-01, M3.pin_2
  N13: S1.M1-02, M3.pin_1
  N14: Part1.POS, Part2.POS
  N15: Part1.NEG, Part2.NEG

notes:
  5.00

custom parts:
  IOXESP32PS: ESP32 Development board By IOXhop
  H-Bridge with L298N: h-bridge
  FC-28 Soil Hygrometer Module - Probe: The FC-28 is a soil hygrometer module that uses the Texas Instruments LM393 comparator chip to provide an analog measurement of soil humidity.
  FC-28 Soil Hygrometer Module: The FC-28 is a soil hygrometer module that uses the Texas Instruments LM393 comparator chip to provide an analog measurement of soil humidity. The digital output is high when soil moisture is over a certain threshold, as determined by adjusting the potentiometer.
  KY-012 Active Buzzer Module: Active Piezoelectric Buzzer Module KY-012, it produces single-tone sound when signal is high. (Special thanks to vanepp for fixing the PCB holes and other errors)
  Hanmatek HM305: DC Power Supply 30V5A HM305.
